// Logisim project Enigma4700.circ as structural Verilog
module HA (
  input  A,
  input  B,
  output S,
  output C
);

  xor xor_1 (S, B, A);
  and and_1 (C, A, B);
endmodule

module FA (
  input  CI,
  input  A,
  input  B,
  output S,
  output CO
);

  wire ha_1_c, ha_2_c, ha_2_s;

  HA ha_1 (.A(CI), .B(ha_2_s), .S(S), .C(ha_1_c));
  HA ha_2 (.A(A), .B(B), .S(ha_2_s), .C(ha_2_c));
  or or_1 (CO, ha_1_c, ha_2_c);
endmodule

module _8BA (
  input  CI,
  input  [7:0] A,
  input  [7:0] B,
  output [7:0] S,
  output CO
);

  wire fa_2_co, fa_3_co, fa_4_co, fa_5_co, fa_6_co, fa_7_co, fa_8_co;

  FA fa_1 (.CI(fa_2_co), .A(A[7]), .B(B[7]), .S(S[7]), .CO(CO));
  FA fa_2 (.CI(fa_3_co), .A(A[6]), .B(B[6]), .S(S[6]), .CO(fa_2_co));
  FA fa_3 (.CI(fa_4_co), .A(A[5]), .B(B[5]), .S(S[5]), .CO(fa_3_co));
  FA fa_4 (.CI(fa_6_co), .A(A[4]), .B(B[4]), .S(S[4]), .CO(fa_4_co));
  FA fa_5 (.CI(fa_7_co), .A(A[2]), .B(B[2]), .S(S[2]), .CO(fa_5_co));
  FA fa_6 (.CI(fa_5_co), .A(A[3]), .B(B[3]), .S(S[3]), .CO(fa_6_co));
  FA fa_7 (.CI(fa_8_co), .A(A[1]), .B(B[1]), .S(S[1]), .CO(fa_7_co));
  FA fa_8 (.CI(CI), .A(A[0]), .B(B[0]), .S(S[0]), .CO(fa_8_co));
endmodule

module INV (
  input  [7:0] in_1,
  input  in_2,
  output [7:0] out_3
);

  xor xor_1 (out_3[7], in_2, in_1[7]);
  xor xor_2 (out_3[6], in_2, in_1[6]);
  xor xor_3 (out_3[5], in_2, in_1[5]);
  xor xor_4 (out_3[4], in_2, in_1[4]);
  xor xor_5 (out_3[3], in_2, in_1[3]);
  xor xor_6 (out_3[2], in_2, in_1[2]);
  xor xor_7 (out_3[1], in_2, in_1[1]);
  xor xor_8 (out_3[0], in_2, in_1[0]);
endmodule

module R_S (
  input  CLR,
  input  R,
  input  S,
  input  PR,
  output Q,
  output Q_prime
);

  nor nor_1 (Q, CLR, R, Q_prime);
  nor nor_2 (Q_prime, Q, S, PR);
endmodule

module D (
  input  CLR,
  input  EN,
  input  D,
  input  PR,
  output Q,
  output Q_prime
);

  wire and_1_out, and_2_out, not_1_out;

  not not_1 (not_1_out, D);
  and and_1 (and_1_out, not_1_out, EN);
  and and_2 (and_2_out, EN, D);
  R_S r_s_1 (.R(and_1_out), .S(and_2_out), .CLR(CLR), .PR(PR), .Q(Q), .Q_prime(Q_prime));
endmodule

module D_2 (
  input  CLR,
  input  D,
  input  CP,
  input  PR,
  output Q,
  output Q_prime
);

  wire d_1_q, not_1_out;

  D d_1 (.EN(not_1_out), .D(D), .Q(d_1_q), .PR(PR), .CLR(CLR));  // open: Q_prime
  not not_1 (not_1_out, CP);
  D d_2 (.EN(CP), .D(d_1_q), .Q(Q), .Q_prime(Q_prime), .PR(PR), .CLR(CLR));
endmodule

module T (
  input  CLR,
  input  CP,
  input  PR,
  output Q,
  output Q_prime
);

  D_2 d_1 (.D(Q_prime), .CP(CP), .CLR(CLR), .PR(PR), .Q(Q), .Q_prime(Q_prime));
endmodule

module _8CT (
  input  CLR,
  input  CP,
  input  EN,
  input  PR,
  output [7:0] O
);

  wire and_1_out, t_1_q_prime, t_2_q_prime, t_3_q_prime, t_4_q_prime, t_5_q_prime, t_6_q_prime, t_7_q_prime;

  and and_1 (and_1_out, CP, EN);
  T t_1 (.CP(and_1_out), .CLR(CLR), .PR(PR), .Q(O[0]), .Q_prime(t_1_q_prime));
  T t_2 (.CP(t_1_q_prime), .CLR(CLR), .PR(PR), .Q(O[1]), .Q_prime(t_2_q_prime));
  T t_3 (.CP(t_4_q_prime), .CLR(CLR), .PR(PR), .Q(O[3]), .Q_prime(t_3_q_prime));
  T t_4 (.CP(t_2_q_prime), .CLR(CLR), .PR(PR), .Q(O[2]), .Q_prime(t_4_q_prime));
  T t_5 (.CP(t_3_q_prime), .CLR(CLR), .PR(PR), .Q(O[4]), .Q_prime(t_5_q_prime));
  T t_6 (.CP(t_5_q_prime), .CLR(CLR), .PR(PR), .Q(O[5]), .Q_prime(t_6_q_prime));
  T t_7 (.CP(t_6_q_prime), .CLR(CLR), .PR(PR), .Q(O[6]), .Q_prime(t_7_q_prime));
  T t_8 (.CP(t_7_q_prime), .CLR(CLR), .PR(PR), .Q(O[7]));  // open: Q_prime
endmodule

module BYTE (
  input  [7:0] DI,
  input  CLR,
  input  PR,
  input  CP,
  output [7:0] DO
);

  D_2 d_1 (.D(DI[0]), .CP(CP), .CLR(CLR), .PR(PR), .Q(DO[0]));  // open: Q_prime
  D_2 d_2 (.D(DI[1]), .CP(CP), .CLR(CLR), .PR(PR), .Q(DO[1]));  // open: Q_prime
  D_2 d_3 (.D(DI[2]), .CP(CP), .CLR(CLR), .PR(PR), .Q(DO[2]));  // open: Q_prime
  D_2 d_4 (.D(DI[3]), .CP(CP), .CLR(CLR), .PR(PR), .Q(DO[3]));  // open: Q_prime
  D_2 d_5 (.D(DI[4]), .CP(CP), .CLR(CLR), .PR(PR), .Q(DO[4]));  // open: Q_prime
  D_2 d_6 (.D(DI[6]), .CP(CP), .CLR(CLR), .PR(PR), .Q(DO[6]));  // open: Q_prime
  D_2 d_7 (.D(DI[5]), .CP(CP), .CLR(CLR), .PR(PR), .Q(DO[5]));  // open: Q_prime
  D_2 d_8 (.D(DI[7]), .CP(CP), .CLR(CLR), .PR(PR), .Q(DO[7]));  // open: Q_prime
endmodule

module GATE (
  input  [7:0] DI,
  input  EN,
  output [7:0] DO
);

  assign DO[7] = EN ? DI[7] : 1'bz;  // Controlled_Buffer controlled_buffer_1
  assign DO[6] = EN ? DI[6] : 1'bz;  // Controlled_Buffer controlled_buffer_2
  assign DO[5] = EN ? DI[5] : 1'bz;  // Controlled_Buffer controlled_buffer_3
  assign DO[4] = EN ? DI[4] : 1'bz;  // Controlled_Buffer controlled_buffer_4
  assign DO[3] = EN ? DI[3] : 1'bz;  // Controlled_Buffer controlled_buffer_5
  assign DO[2] = EN ? DI[2] : 1'bz;  // Controlled_Buffer controlled_buffer_6
  assign DO[1] = EN ? DI[1] : 1'bz;  // Controlled_Buffer controlled_buffer_7
  assign DO[0] = EN ? DI[0] : 1'bz;  // Controlled_Buffer controlled_buffer_8
endmodule

module REG (
  input  [7:0] DI,
  input  CLR,
  input  PR,
  input  CP,
  input  WE,
  input  CS,
  output [7:0] S,
  output [7:0] DO
);

  wire and_1_out, and_2_out, not_1_out;

  and and_1 (and_1_out, CP, CS, WE);
  BYTE byte_1 (.DI(DI), .CLR(CLR), .PR(PR), .CP(and_1_out), .DO(S));
  GATE gate_1 (.DI(S), .EN(and_2_out), .DO(DO));
  and and_2 (and_2_out, not_1_out, CS);
  not not_1 (not_1_out, WE);
endmodule

module _8x1 (
  input  [7:0] DI,
  input  CLR,
  input  PR,
  input  CP,
  input  WE,
  input  [2:0] A,
  input  CS,
  output [7:0] DO
);

  wire [7:0] n38dec_1_o;

  _38DEC u_38dec_1 (.A2(A[2]), .A1(A[1]), .A0(A[0]), .EN(CS), .O(n38dec_1_o));
  REG reg_1 (.DI(DI), .CLR(CLR), .PR(PR), .CP(CP), .WE(WE), .CS(n38dec_1_o[7]), .DO(DO));  // open: S
  REG reg_2 (.DI(DI), .CLR(CLR), .PR(PR), .CP(CP), .WE(WE), .CS(n38dec_1_o[6]), .DO(DO));  // open: S
  REG reg_3 (.DI(DI), .CLR(CLR), .PR(PR), .CP(CP), .WE(WE), .CS(n38dec_1_o[5]), .DO(DO));  // open: S
  REG reg_4 (.DI(DI), .CLR(CLR), .PR(PR), .CP(CP), .WE(WE), .CS(n38dec_1_o[4]), .DO(DO));  // open: S
  REG reg_5 (.DI(DI), .CLR(CLR), .PR(PR), .CP(CP), .WE(WE), .CS(n38dec_1_o[3]), .DO(DO));  // open: S
  REG reg_6 (.DI(DI), .CLR(CLR), .PR(PR), .WE(WE), .CS(n38dec_1_o[2]), .DO(DO));  // open: CP, S
  REG reg_7 (.DI(DI), .CLR(CLR), .PR(PR), .CP(CP), .WE(WE), .CS(n38dec_1_o[1]), .DO(DO));  // open: S
  REG reg_8 (.DI(DI), .CLR(CLR), .PR(PR), .CP(CP), .WE(WE), .CS(n38dec_1_o[0]), .DO(DO));  // open: S
endmodule

module _38DEC (
  input  A2,
  input  A1,
  input  A0,
  input  EN,
  output [7:0] O
);

  wire not_1_out, not_2_out, not_3_out;

  not not_1 (not_1_out, A2);
  not not_2 (not_2_out, A1);
  not not_3 (not_3_out, A0);
  and and_1 (O[7], A2, A1, A0, EN);
  and and_2 (O[6], A2, A1, not_3_out, EN);
  and and_3 (O[5], A2, not_2_out, A0, EN);
  and and_4 (O[4], A2, not_2_out, not_3_out, EN);
  and and_5 (O[3], not_1_out, A1, A0, EN);
  and and_6 (O[2], not_1_out, A1, not_3_out, EN);
  and and_7 (O[1], not_1_out, not_2_out, A0, EN);
  and and_8 (O[0], not_1_out, not_2_out, not_3_out, EN);
endmodule

module _2x8 (
  input  [15:0] DI,
  input  CLR,
  input  PR,
  input  CP,
  input  [2:0] A,
  input  WE,
  input  CS,
  output [15:0] DO
);

  _8x1 u_8x1_1 (.DI(DI[15:8]), .CLR(CLR), .PR(PR), .CP(CP), .A(A), .CS(CS), .DO(DO[15:8]), .WE(WE));
  _8x1 u_8x1_2 (.DI(DI[7:0]), .CLR(CLR), .PR(PR), .CP(CP), .A(A), .CS(CS), .DO(DO[7:0]), .WE(WE));
endmodule

module _3CT (
  input  CLR,
  input  EN,
  input  PR,
  input  CP,
  output [2:0] O
);

  wire [7:3] n8ct_1_o;

  _8CT u_8ct_1 (.O({n8ct_1_o, O}), .CLR(CLR), .CP(CP), .PR(PR), .EN(EN));
endmodule

module ALU (
  input  [7:0] A,
  input  [7:0] B,
  input  [2:0] OP,
  input  EN,
  input  CLR,
  input  PR,
  input  CP,
  output [7:0] S,
  output [7:0] O,
  output [2:0] PSW
);

  wire and_1_out, and_2_out, n8ba_1_co, n8ba_2_co;
  wire [1:0] or_1_out;
  wire [7:0] inv_1_out_3, inv_2_out_3, n8and_1_o, n8ba_1_s, n8ba_2_s, n8or_1_o, n8xor_1_o, n38dec_1_o;
  wire [7:3] reg_1_s;

  _38DEC u_38dec_1 (.A2(OP[2]), .A1(OP[1]), .A0(OP[0]), .EN(1'b1), .O(n38dec_1_o));
  _8BA u_8ba_1 (.CI(1'b0), .A(A), .B(B), .S(n8ba_1_s), .CO(n8ba_1_co));
  GATE gate_1 (.DI(n8ba_1_s), .EN(n38dec_1_o[0]), .DO(S));
  _8BA u_8ba_2 (.CI(1'b1), .A(A), .B(inv_1_out_3), .S(n8ba_2_s), .CO(n8ba_2_co));
  GATE gate_2 (.DI(n8ba_2_s), .EN(n38dec_1_o[1]), .DO(S));
  and and_1 (and_1_out, n38dec_1_o[0], n8ba_1_co);
  INV inv_1 (.in_1(B), .in_2(1'b1), .out_3(inv_1_out_3));
  and and_2 (and_2_out, n38dec_1_o[1], n8ba_2_co);
  nor nor_1 (or_1_out[1], S[0], S[1], S[2], S[3], S[4], S[5], S[6], S[7]);
  _8AND u_8and_1 (.A(A), .B(B), .O(n8and_1_o));
  GATE gate_3 (.DI(n8and_1_o), .EN(n38dec_1_o[2]), .DO(S));
  or or_1 (or_1_out[0], and_2_out, and_1_out);
  _8OR u_8or_1 (.A(A), .B(B), .O(n8or_1_o));
  GATE gate_4 (.DI(n8or_1_o), .EN(n38dec_1_o[3]), .DO(S));
  GATE gate_5 (.DI(n8xor_1_o), .EN(n38dec_1_o[4]), .DO(S));
  REG reg_1 (
    .DI({{5{1'b0}}, S[0], or_1_out}), .CLR(CLR), .PR(PR), .CP(CP), .WE(1'b1), .CS(1'b1), .S({reg_1_s, PSW}));  // open: DO
  _8XOR u_8xor_1 (.A(A), .B(B), .O(n8xor_1_o));
  GATE gate_6 (.DI(inv_2_out_3), .EN(n38dec_1_o[5]), .DO(S));
  INV inv_2 (.in_1(A), .in_2(1'b1), .out_3(inv_2_out_3));
  GATE gate_7 (.DI(S), .EN(EN), .DO(O));
endmodule

module POW (
  input  RES,
  input  POW,
  input  MAN,
  input  PUL,
  input  HLT,
  output CP,
  output RES_2
);

  wire and_1_out, and_2_out, and_3_out, clock_1_out, not_1_out, not_2_out, not_3_out, not_4_out, not_5_out;

  Clock clock_1 (.out(clock_1_out));
  not not_1 (not_1_out, RES);
  not not_2 (not_2_out, POW);
  not not_3 (not_3_out, MAN);
  not not_4 (not_4_out, PUL);
  not not_5 (not_5_out, HLT);
  and and_1 (and_1_out, POW, not_1_out, not_3_out, not_5_out, clock_1_out);
  and and_2 (and_2_out, POW, not_1_out, MAN, not_5_out, PUL);
  or or_1 (CP, and_1_out, and_2_out);
  and and_3 (and_3_out, POW, RES);
  or or_2 (RES_2, and_3_out, not_2_out);

  // Notes on the sheet:
  //   RESET
  //   POWER
  //   MANUAL
  //   PULSE
  //   HALT
  //   CLOCK
endmodule

module PC (
  input  [7:0] DI,
  input  CLR,
  input  WE,
  input  PR,
  input  CS,
  input  CP,
  input  EN,
  output [7:0] DO,
  output [7:0] S
);

  wire not_1_out;
  wire [7:0] gate_1_do, n8ba_1_s;

  not not_1 (not_1_out, EN);
  GATE gate_1 (.DI(DI), .EN(not_1_out), .DO(gate_1_do));
  REG reg_1 (.DI(gate_1_do), .CLR(CLR), .PR(PR), .CP(CP), .WE(WE), .CS(CS), .DO(DO), .S(S));
  _8BA u_8ba_1 (.CI(1'b0), .A(S), .B(8'h1), .S(n8ba_1_s));  // open: CO
  GATE gate_2 (.DI(n8ba_1_s), .EN(EN), .DO(gate_1_do));
endmodule

module MC (
  input  [7:0] DI,
  input  CP,
  input  WE,
  input  CS,
  output W,
  output [7:0] S,
  output [7:0] DO
);

  wire and_2_out, not_1_out;

  and and_1 (W, CP, WE, CS);
  GATE gate_1 (.DI(DI), .EN(and_2_out), .DO(DO));
  and and_2 (and_2_out, not_1_out, CS);
  not not_1 (not_1_out, WE);

  assign S = DI;
endmodule

module EW (
  input  [7:0] in_1,
  input  in_2,
  output [7:0] DO
);

  GATE gate_1 (.DI(in_1), .EN(in_2), .DO(DO));
endmodule

module _8AND (
  input  [7:0] A,
  input  [7:0] B,
  output [7:0] O
);

  and and_1 (O[0], B[0], A[0]);
  and and_2 (O[1], B[1], A[1]);
  and and_3 (O[2], B[2], A[2]);
  and and_4 (O[3], B[3], A[3]);
  and and_5 (O[4], B[4], A[4]);
  and and_6 (O[5], B[5], A[5]);
  and and_7 (O[6], B[6], A[6]);
  and and_8 (O[7], B[7], A[7]);
endmodule

module _8OR (
  input  [7:0] A,
  input  [7:0] B,
  output [7:0] O
);

  or or_1 (O[0], B[0], A[0]);
  or or_2 (O[1], B[1], A[1]);
  or or_3 (O[2], B[2], A[2]);
  or or_4 (O[3], B[3], A[3]);
  or or_5 (O[4], B[4], A[4]);
  or or_6 (O[5], B[5], A[5]);
  or or_7 (O[6], B[6], A[6]);
  or or_8 (O[7], B[7], A[7]);
endmodule

module _8XOR (
  input  [7:0] A,
  input  [7:0] B,
  output [7:0] O
);

  xor xor_1 (O[0], B[0], A[0]);
  xor xor_2 (O[1], B[1], A[1]);
  xor xor_3 (O[2], B[2], A[2]);
  xor xor_4 (O[3], B[3], A[3]);
  xor xor_5 (O[4], B[4], A[4]);
  xor xor_6 (O[5], B[5], A[5]);
  xor xor_7 (O[6], B[6], A[6]);
  xor xor_8 (O[7], B[7], A[7]);
endmodule

module RC (
  input  [4:0] W,
  input  [4:0] R,
  output [1:0] CS,
  output [1:0] A,
  output [1:0] DS,
  output [1:0] B,
  output [1:0] MSR,
  output [1:0] SS,
  output [1:0] C,
  output [1:0] MAR,
  output [1:0] ES,
  output [1:0] D,
  output [1:0] MDR,
  output [1:0] VEC,
  output [1:0] DI,
  output [1:0] MC,
  output [1:0] T1,
  output [1:0] SI,
  output [1:0] IR,
  output [1:0] T2,
  output [1:0] SP,
  output [1:0] DST,
  output [1:0] BP,
  output [1:0] SRC
);

  wire [31:0] n32xor_1_out_3, n532dec_1_d, n532dec_2_d;

  _532DEC u_532dec_1 (
    .A(W),
    .D({n532dec_1_d[31:23], T2[0], T1[0], VEC[0], ES[0], SS[0], DS[0], CS[0], BP[0], SP[0], SI[0], DI[0], D[0], C[0], B[0], A[0], SRC[0], DST[0], IR[0], MC[0], MDR[0], MAR[0], MSR[0], n532dec_1_d[0]}));
  _532DEC u_532dec_2 (.A(R), .D(n532dec_2_d));
  _32XOR u_32xor_1 (
    .A({n532dec_1_d[31:23], T2[0], T1[0], VEC[0], ES[0], SS[0], DS[0], CS[0], BP[0], SP[0], SI[0], DI[0], D[0], C[0], B[0], A[0], SRC[0], DST[0], IR[0], MC[0], MDR[0], MAR[0], MSR[0], n532dec_1_d[0]}),
    .B(n532dec_2_d),
    .out_3({n32xor_1_out_3[31:23], T2[1], T1[1], VEC[1], ES[1], SS[1], DS[1], CS[1], BP[1], SP[1], SI[1], DI[1], D[1], C[1], B[1], A[1], SRC[1], DST[1], IR[1], MC[1], MDR[1], MAR[1], MSR[1], n32xor_1_out_3[0]}));
endmodule

module _532DEC (
  input  [4:0] A,
  output [31:0] D
);

  ROM #(.addrWidth(5), .dataWidth(32)) rom_1 (.addr(A), .data(D));  // open: sel

  // Notes on the sheet:
  //   contents of rom_1 (hex, n*v repeats v):
  //   1 2 4 8 10 20 40 80 100 200 400 800 1000 2000 4000 8000 10000 20000 40000 80000 100000 200000 400000
  //   800000 1000000 2000000 4000000 8000000 10000000 20000000 40000000 80000000
endmodule

module _32XOR (
  input  [31:0] A,
  input  [31:0] B,
  output [31:0] out_3
);

  _8XOR u_8xor_1 (.A(A[7:0]), .B(B[7:0]), .O(out_3[7:0]));
  _8XOR u_8xor_2 (.A(A[15:8]), .B(B[15:8]), .O(out_3[15:8]));
  _8XOR u_8xor_3 (.A(A[23:16]), .B(B[23:16]), .O(out_3[23:16]));
  _8XOR u_8xor_4 (.A(A[31:24]), .B(B[31:24]), .O(out_3[31:24]));
endmodule
